// Logisim project cpu.circ as structural Verilog: 1 circuit, main circuit main
module main (
  input  [31:0] INSTRUCTION,
  input  CLOCK,
  output [31:0] FETCH_ADDRESS,
  output [31:0] s0_Value,
  output [31:0] s1_Value,
  output [31:0] s2_Value,
  output [31:0] ra_Value,
  output [31:0] sp_Value
);

  wire clkl, mem_to_reg, regfile_1_p1, RegWrite;
  wire [3:0] alucontrol;
  wire [23:0] bit_extender_2_out;
  wire [31:0] bit_extender_1_out, main_1_result, ram_1_data, regfile_1_p3, regfile_1_p5, regfile_1_p7;

  // regfile regfile_1: pin names not known; wires that end beside it: regfile_1_p1, RegWrite, regfile_1_p3, INSTRUCTION[25:21], regfile_1_p5, INSTRUCTION[20:16], regfile_1_p7, sp_Value, ra_Value, s2_Value, s1_Value, s0_Value, CLOCK
  assign bit_extender_1_out = {{16{INSTRUCTION[15]}}, INSTRUCTION[15:0]};  // Bit_Extender bit_extender_1
  alu_main main_1 (
    .Switch(alucontrol), .X(regfile_1_p5), .Result(main_1_result), .Y(bit_extender_1_out));  // open: Equal, Signed_Overflow
  Bit_Extender #(.in_width(32), .out_width(24)) bit_extender_2 (.in(main_1_result), .out(bit_extender_2_out));
  RAM #(.addrWidth(24), .dataWidth(32), .bus("separate")) ram_1 (
    .addr(bit_extender_2_out), .din(regfile_1_p7), .data(ram_1_data), .clk(clkl));  // open: str, sel, ld, clr
  Multiplexer #(.width(32)) multiplexer_1 (
    .in0(main_1_result), .in1(ram_1_data), .out(regfile_1_p3), .sel(mem_to_reg));  // open: en

  // Other names for the same wires on the sheet: clk = CLOCK; fetch_addr[31:0] = FETCH_ADDRESS; ra[31:0] = ra_Value;
  //   s0[31:0] = s0_Value; s1[31:0] = s1_Value; s2[31:0] = s2_Value; sp[31:0] = sp_Value

  // Notes on the sheet:
  //   Output
  //   These are outputs/inputs from run.circ
  //   Inputs
  //   These are DEBUG/TEST outputs from your circuit.
endmodule
